// Digital circuit half_adder.dig as structural Verilog
module half_adder (
);

  wire and_1_out, switch_1_b, switch_2_b, xor_1_out;

  Switch switch_1 (.A(1'b1), .B(switch_1_b));
  Switch switch_2 (.A(1'b1), .B(switch_2_b));
  PullDown pulldown_1 (.out(switch_1_b));
  PullDown pulldown_2 (.out(switch_2_b));
  xor xor_1 (xor_1_out, switch_1_b, switch_2_b);
  and and_1 (and_1_out, switch_2_b, switch_1_b);
  LED led_1 (.in(xor_1_out));
  LED led_2 (.in(and_1_out));
endmodule
