// Digital circuit first_test.dig as structural Verilog
module first_test (
);

  wire nand_1_out, switch_1_b, switch_2_b;

  Switch switch_1 (.A(1'b1), .B(switch_1_b));
  Switch switch_2 (.A(1'b1), .B(switch_2_b));
  nand nand_1 (nand_1_out, switch_1_b, switch_2_b);
  PullDown pulldown_1 (.out(switch_2_b));
  PullDown pulldown_2 (.out(switch_1_b));
  LED led_1 (.in(nand_1_out));
endmodule
